// Logisim project 10.circ as structural Verilog: 3 circuits, main circuit main
module main (
  input  X,
  input  Y,
  input  Z,
  output P,
  output S,
  output C,
  output G
);

  wire and_2_out;

  and and_1 (G, Y, X);
  xor xor_1 (P, X, Y);
  xor xor_2 (S, P, Z);
  and and_2 (and_2_out, Z, P);
  or or_1 (C, and_2_out, G);
endmodule

module CARRY (
  input  X0,
  input  X1,
  input  X2,
  input  X3,
  input  Y0,
  input  Y1,
  input  Y2,
  input  Y3,
  input  C0,
  output C4,
  output S0,
  output S1,
  output S2,
  output S3
);

  wire and_1_out, and_2_out, and_3_out, and_4_out, and_5_out, and_6_out, and_7_out, and_8_out, and_9_out,
       and_10_out, and_11_out, main_1_g, main_1_p, main_2_g, main_2_p, main_3_g, main_3_p, main_4_g,
       main_4_p, or_1_out, or_2_out, or_3_out, or_4_out;

  main main_1 (.X(X0), .Y(Y0), .Z(C0), .P(main_1_p), .S(S0), .G(main_1_g));  // open: C
  and and_1 (and_1_out, main_1_p, C0);
  or or_1 (or_1_out, and_1_out, main_1_g);
  main main_2 (.X(X1), .Y(Y1), .Z(or_1_out), .P(main_2_p), .S(S1), .G(main_2_g));  // open: C
  and and_2 (and_2_out, main_1_p, main_2_p);
  and and_3 (and_3_out, main_1_g, main_2_p);
  and and_4 (and_4_out, C0, and_2_out);
  or or_2 (or_2_out, and_3_out, main_2_g);
  or or_3 (or_3_out, and_4_out, or_2_out);
  main main_3 (.X(X2), .Y(Y2), .Z(or_3_out), .P(main_3_p), .S(S2), .G(main_3_g));  // open: C
  and and_5 (and_5_out, main_1_g, main_2_p, main_3_p);
  and and_6 (and_6_out, main_2_g, main_3_p);
  and and_7 (and_7_out, main_1_p, C0, main_2_p, main_3_p);
  or or_4 (or_4_out, and_5_out, and_7_out, main_3_g, and_6_out);
  main main_4 (.X(X3), .Y(Y3), .Z(or_4_out), .P(main_4_p), .S(S3), .G(main_4_g));  // open: C
  and and_8 (and_8_out, main_3_g, main_4_p);
  and and_9 (and_9_out, main_2_g, main_3_p, main_4_p);
  and and_10 (and_10_out, main_2_p, main_3_p, main_2_g, main_4_p);
  and and_11 (and_11_out, C0, main_3_p, main_2_p, main_1_p, main_4_p);
  or or_5 (C4, and_11_out, and_10_out, and_9_out, and_8_out, main_4_g);
endmodule

module CARRYADD (
  input  [3:0] X,
  input  [3:0] Y,
  input  C0
);

  wire [0:0] carry_1_c4;
  wire [3:0] carry_1_s0;

  CARRY carry_1 (
    .X0(X[0]), .X1(X[1]), .X2(X[2]), .X3(X[3]), .Y0(Y[0]), .Y1(Y[1]), .Y2(Y[2]), .Y3(Y[3]), .C0(C0),
    .C4(carry_1_c4[0]), .S0(carry_1_s0[0]), .S1(carry_1_s0[1]), .S2(carry_1_s0[2]), .S3(carry_1_s0[3]));
  Hex_Digit_Display hex_digit_display_1 (.value(carry_1_s0));  // open: dp
  Hex_Digit_Display hex_digit_display_2 (.value({{3{C0}}, carry_1_c4[0]}));  // open: dp
endmodule
